# Fritzing sketch dev (saved by Fritzing 1.0.3b)
breadboards: 1

parts:
  S3 = Pushbutton [package="[THT]"]
  S4 = Pushbutton [package="[THT]"]
  S5 = Pushbutton [package="[THT]"]
  A1 = XIAO ESP32C3-smd
  U1 = Mini-360 DC-DC Buck converter [package=THT]
  D1 = Schottky Diode [part_number=1N5817 package="300 mil [THT]"]
  J1 = Camdenboss CTB0158-2 [part_number=CTB0158-2 package=THT]
  J2 = Camdenboss CTB0158-2 [part_number=CTB0158-2 package=THT]
  J3 = Camdenboss CTB0158-2 [part_number=CTB0158-2 package=THT]
  Q1 = TRANSISTOR_NPN [package=to-92-ammo]
  Q2 = TRANSISTOR_NPN [package=to-92-ammo]
  Q3 = TRANSISTOR_NPN [package=to-92-ammo]
  Q4 = TRANSISTOR_NPN [package=to-92-ammo]
  R1 = Resistor [tolerance=±5% resistance=4.7k package="0603 [SMD]"]
  R2 = Resistor [tolerance=±5% resistance=4.7k package="0805 [SMD]"]
  D2 = Schottky Diode [part_number=1N5817 package="300 mil [THT]"]

nets:
  N1: S3.Pin_1, S3.Pin_2, A1.Pin_17
  N2: S3.Pin_3, S3.Pin_4, S4.Pin_3, S4.Pin_4, S5.Pin_3, S5.Pin_4, A1.Pin_2, A1.Pin_21, U1.OUT-, Q1.E, Q2.E, Q3.E, Q4.E
  N3: S4.Pin_1, S4.Pin_2, A1.Pin_18
  N4: S5.Pin_1, S5.Pin_2, A1.Pin_19
  N5: A1.Pin_12, R2.Pin_0
  N6: A1.Pin_14, R1.Pin_0
  N7: A1.Pin_22, D1.cathode
  N8: U1.IN-, D2.anode
  N9: U1.IN+, J1.pin1, J2.pin1, J3.pin1
  N10: U1.OUT+, D1.anode
  N11: J1.pin2, D2.cathode
  N12: J2.pin2, Q1.C, Q2.C
  N13: J3.pin2, Q3.C, Q4.C
  N14: Q1.B, Q2.B, R1.Pin_1
  N15: Q3.B, Q4.B, R2.Pin_1

custom parts:
  XIAO ESP32C3-smd: Seeed Studio XIAO ESP32C3 adopts new RISC-V architecture, supporting both Wi-Fi and BLE wireless connectivities.
  Mini-360 DC-DC Buck converter: Mini-360 DC-DC Buck converter. Tiny buck step down voltage converter, input voltage 4.75 to 23V output 1 to 17V adjustable. Available from ebay and the like.
