# Fritzing sketch dev3 (saved by Fritzing 1.0.3b)
breadboards: 1

parts:
  S3 = Pushbutton [package="[THT]"]
  S4 = Pushbutton [package="[THT]"]
  S5 = Pushbutton [package="[THT]"]
  A1 = XIAO ESP32C3-smd
  U1 = Mini-360 DC-DC Buck converter [package=THT]
  D1 = Schottky Diode [part_number=1N5817 package="300 mil [THT]"]
  Q1 = TRANSISTOR_NPN [package=to-92-ammo]
  Q2 = TRANSISTOR_NPN [package=to-92-ammo]
  Q3 = TRANSISTOR_NPN [package=to-92-ammo]
  Q4 = TRANSISTOR_NPN [package=to-92-ammo]
  R2 = Resistor [tolerance=±5% resistance=4.7k package="0805 [SMD]"]
  D2 = Schottky Diode [part_number=1N5817 package="300 mil [THT]"]
  R3 = Resistor [tolerance=±5% resistance=4.7k package="0805 [SMD]"]
  Q5 = TRANSISTOR_NPN [package=to-92-ammo]
  R4 = Resistor [tolerance=±5% resistance=4.7k package="0805 [SMD]"]
  Q6 = TRANSISTOR_NPN [package=to-92-ammo]

nets:
  N1: S3.Pin_1, S3.Pin_2, A1.Pin_17
  N2: S3.Pin_3, S3.Pin_4, S4.Pin_3, S4.Pin_4, S5.Pin_3, S5.Pin_4, A1.Pin_2, A1.Pin_19, A1.Pin_21, U1.IN-, Q3.E, Q4.E, Q5.E, Q6.E
  N3: S4.Pin_1, S4.Pin_2, A1.Pin_16
  N4: S5.Pin_1, S5.Pin_2, A1.Pin_15
  N5: A1.Pin_11, R4.Pin_0
  N6: A1.Pin_12, R2.Pin_0
  N7: A1.Pin_14, R3.Pin_0
  N8: A1.Pin_22, D1.cathode
  N9: U1.IN+, D2.cathode
  N10: U1.OUT+, D1.anode
  N11: U1.OUT-, Q1.E, Q2.E
  N12: Q1.B, Q2.B, R3.Pin_1
  N13: Q1.C, Q2.C
  N14: Q3.B, Q4.B, R2.Pin_1
  N15: Q3.C, Q4.C
  N16: Q5.B, R4.Pin_1, Q6.B
  N17: Q5.C, Q6.C

notes:
  V+
  V-
  G
  R
  B

custom parts:
  XIAO ESP32C3-smd: Seeed Studio XIAO ESP32C3 adopts new RISC-V architecture, supporting both Wi-Fi and BLE wireless connectivities.
  Mini-360 DC-DC Buck converter: Mini-360 DC-DC Buck converter. Tiny buck step down voltage converter, input voltage 4.75 to 23V output 1 to 17V adjustable. Available from ebay and the like.
