# Fritzing sketch rgb-controller (saved by Fritzing 1.0.3b)
breadboards: 1

parts:
  S3 = Pushbutton [package="[THT]"]
  S4 = Pushbutton [package="[THT]"]
  S5 = Pushbutton [package="[THT]"]
  U1 = Mini-360 DC-DC Buck converter [package=THT]
  D1 = Schottky Diode [part_number=1N5817 package="300 mil [THT]"]
  Q1 = TRANSISTOR_NPN [package=to-92-ammo]
  Q2 = TRANSISTOR_NPN [package=to-92-ammo]
  Q3 = TRANSISTOR_NPN [package=to-92-ammo]
  Q4 = TRANSISTOR_NPN [package=to-92-ammo]
  R2 = Resistor [tolerance=±5% resistance=4.7k package="0805 [SMD]"]
  D2 = Schottky Diode [part_number=1N5817 package="300 mil [THT]"]
  R3 = Resistor [tolerance=±5% resistance=4.7k package="0805 [SMD]"]
  Q5 = TRANSISTOR_NPN [package=to-92-ammo]
  R4 = Resistor [tolerance=±5% resistance=4.7k package="0805 [SMD]"]
  Q6 = TRANSISTOR_NPN [package=to-92-ammo]
  Mod1 = seeeduino-xiao

nets:
  N1: S3.Pin_1, S3.Pin_2, Mod1.D8
  N2: S3.Pin_3, S3.Pin_4, S4.Pin_3, S4.Pin_4, S5.Pin_3, S5.Pin_4, U1.IN-, Q1.E, Q2.E, Q3.E, Q4.E, Q5.E, Q6.E, Mod1.GND
  N3: S4.Pin_1, S4.Pin_2, Mod1.D7
  N4: S5.Pin_1, S5.Pin_2, Mod1.D6
  N5: U1.IN+, D2.cathode
  N6: U1.OUT+, D1.anode
  N7: D1.cathode, Mod1.5V
  N8: Q1.B, Q2.B, R3.Pin_1
  N9: Q1.C, Q2.C
  N10: Q3.B, Q4.B, R2.Pin_1
  N11: Q3.C, Q4.C
  N12: R2.Pin_0, Mod1.D3
  N13: R3.Pin_0, Mod1.D5
  N14: Q5.B, R4.Pin_1, Q6.B
  N15: Q5.C, Q6.C
  N16: R4.Pin_0, Mod1.D2

notes:
  V+
  V-
  G
  R
  B

custom parts:
  Mini-360 DC-DC Buck converter: Mini-360 DC-DC Buck converter. Tiny buck step down voltage converter, input voltage 4.75 to 23V output 1 to 17V adjustable. Available from ebay and the like.
  seeeduino-xiao: Seeeduino XIAO processor board.
